// Digital circuit ALU8bits.dig as structural Verilog
module ALU8bits (
  input  [2:0] Opcode,
  input  [7:0] B,
  input  [7:0] A,
  output [7:0] RAC,
  output [7:0] RMQ
);

  wire Cout;
  wire [7:0] AC, MQ, N, Q, R, S, SL, SR, X;

  shiftleftac8bits shiftleftac8bits_1 (
    .A(A), .B(B), .Op(Opcode[0]), .Cout(Cout), .NAND8BITS(N), .XOR8BITS(X), .SHIFTRIGHT(SR), .SHIFTLEFT(SL),
    .S(S));
  registradores8bits registradores8bits_1 (.A(A), .B(B), .AC(AC), .MQ(MQ));
  divisor8bits divisor8bits_1 (.Dividendo(A), .Divisor(B), .R(R), .Q(Q));
  Multiplexer #(.Selector_Bits(3), .Bits(8)) multiplexer_1 (
    .sel(Opcode), .in_0(S), .in_1(S), .in_2(AC), .in_3(R), .in_4(SR), .in_5(SL), .in_6({8{1'b0}}),
    .in_7({8{1'b0}}), .out(RAC));
  Multiplexer #(.Selector_Bits(3), .Bits(8)) multiplexer_2 (
    .sel(Opcode), .in_0({8{1'b0}}), .in_1({8{1'b0}}), .in_2(MQ), .in_3(Q), .in_4({8{1'b0}}),
    .in_5({8{1'b0}}), .in_6({8{1'b0}}), .in_7({8{1'b0}}), .out(RMQ));

  // Other names for the same wires on the sheet: Op[2:0] = Opcode; Op1 = Opcode[0]; Op2 = Opcode[1]; Op3 = Opcode[2]
endmodule
