// Digital circuit CPU8BITS.dig as structural Verilog
module CPU8BITS (
  input  CLOCK,
  output [7:0] MOUT,
  output [7:0] AOUT
);

  wire AC_IN, ALU_OP0, ALU_OP1, ALU_OP2, B_IN;
  wire [7:0] A, AD, BD, BUS, D, EP, RAC, RMQ;
  wire [7:5] Q;
  wire [14:0] DP;

  ROM #(.AddrBits(8), .Bits(16)) CONTROLE (
    .A(EP), .sel(1'b1), .D({B_IN, DP[14], ALU_OP2, ALU_OP1, ALU_OP0, DP[10:8], AC_IN, DP[6:0]}));
  CounterPreset #(.Bits(8)) counterpreset_1 (
    .en(DP[2]), .C(CLOCK), .dir(1'b0), .in(BUS), .ld(DP[1]), .clr(1'b0), .out(A));  // open: ovf
  ROM #(.AddrBits(8), .Bits(8)) PRINCIPAL (.A(AD), .sel(1'b1), .D(D));
  Register #(.Bits(8)) IR (.D(BUS), .C(CLOCK), .en(DP[5]), .Q({Q, EP[7:3]}));
  ALU8bits alu8bits_1 (.Opcode(Q), .B(BD), .A(AOUT), .RAC(RAC), .RMQ(RMQ));
  Counter #(.Bits(3)) counter_1 (.en(1'b1), .C(CLOCK), .clr(DP[14]), .out(EP[2:0]));  // open: ovf
  Register #(.Bits(8)) MAR (.D(BUS), .C(CLOCK), .en(DP[3]), .Q(AD));
  Register #(.Bits(8)) B (.D(BUS), .C(CLOCK), .en(B_IN), .Q(BD));
  assign BUS = DP[0] ? A : 8'bz;  // Driver driver_1
  assign BUS = DP[4] ? D : 8'bz;  // Driver driver_2
  assign BUS = DP[6] ? {Q, EP[7:3]} : 8'bz;  // Driver driver_3
  assign BUS = DP[9] ? RAC : 8'bz;  // Driver driver_4
  assign BUS = DP[10] ? RMQ : 8'bz;  // Driver driver_5
  Register #(.Bits(8)) AC (.D(BUS), .C(CLOCK), .en(AC_IN), .Q(AOUT));
  Register #(.Bits(8)) MQ (.D(BUS), .C(CLOCK), .en(DP[8]), .Q(MOUT));

  // Other names for the same wires on the sheet: AC[7:0] = AOUT; CLK = CLOCK; PC_OUT = DP[0]; PC_IN = DP[1];
  //   PC_INC = DP[2]; MAR_IN = DP[3]; ROM_OUT = DP[4]; IR_IN = DP[5]; IR_OUT = DP[6];
  //   DP (some bits) = {B_IN, ALU_OP2, ALU_OP1, ALU_OP0, AC_IN}; MQ_IN = DP[8]; RAC_OUT = DP[9]; RMQ_OUT = DP[10];
  //   STEP_CLR = DP[14]; Op[4:0] = EP[7:3]; Q[4:0] = EP[7:3]; Q1[2:0] = Q; STEP[2:0] = EP[2:0]

  // Notes on the sheet:
  //   contents of CONTROLE (hex, n*v repeats v):
  //   9,22,30,ffa
  //   contents of PRINCIPAL (hex, n*v repeats v):
  //   0,2a
endmodule
