// Digital circuit CPU8BITS_v2.dig as structural Verilog
module CPU8BITS_v2 (
  input  clk,
  input  RESET,
  input  PC_IN,
  output [7:0] MQ_OUT,
  output [7:0] AC_OUT,
  output [7:0] IR_OUT,
  output [2:0] S_OUT,
  output [7:0] MAR_OUT
);

  wire AC_IN, AC_OUT_t, CLR, FIM, IR_IN, MAR_IN, MQ_IN, MQ_OUT_t, N_IN, PC_INC, PC_OUT, RAM_IN, RAM_OUT;
  wire [6:3] eeprom_2_d;
  wire [7:0] ALU_AC, ALU_MQ, BUS, PC_out_2, Q3, rom_1_d;

  Register #(.Bits(8)) MAR (.D(BUS), .C(clk), .en(MAR_IN), .Q(MAR_OUT));
  Register #(.Bits(8)) N (.D(BUS), .C(clk), .en(N_IN), .Q(Q3));
  ROM #(.AddrBits(8), .Bits(8)) rom_1 (.A(MAR_OUT), .sel(1'b1), .D(rom_1_d));
  CounterPreset #(.Bits(8)) PC (
    .en(PC_INC), .C(clk), .dir(1'b0), .in(BUS), .ld(PC_IN), .clr(RESET), .out(PC_out_2));  // open: ovf
  assign BUS = RAM_OUT ? rom_1_d : 8'bz;  // Driver driver_1
  assign BUS = PC_OUT ? PC_out_2 : 8'bz;  // Driver driver_2
  ALU8bits alu8bits_1 (.Opcode(IR_OUT[2:0]), .B(Q3), .A(AC_OUT), .RAC(ALU_AC), .RMQ(ALU_MQ));
  or or_1 (CLR, FIM, RESET);
  Register #(.Bits(8)) AC (.D(ALU_AC), .C(clk), .en(AC_IN), .Q(AC_OUT));
  Register #(.Bits(8)) MQ (.D(ALU_MQ), .C(clk), .en(MQ_IN), .Q(MQ_OUT));
  Register #(.Bits(8)) IR (.D(BUS), .C(clk), .en(IR_IN), .Q(IR_OUT));
  assign BUS = AC_OUT_t ? AC_OUT : 8'bz;  // Driver driver_3
  assign BUS = MQ_OUT_t ? MQ_OUT : 8'bz;  // Driver driver_4
  CounterPreset #(.Bits(3)) STEP (
    .en(1'b1), .C(clk), .dir(FIM), .in(3'b000), .ld(1'b0), .clr(CLR), .out(S_OUT));  // open: ovf
  EEPROM #(.AddrBits(6), .Bits(8)) eeprom_1 (
    .A({IR_OUT[2:0], S_OUT}), .CS(1'b1), .WE(1'b0), .OE(1'b1),
    .D({AC_OUT_t, AC_IN, N_IN, PC_INC, IR_IN, RAM_OUT, MAR_IN, PC_OUT}));
  EEPROM #(.AddrBits(6), .Bits(8)) eeprom_2 (
    .A({IR_OUT[2:0], S_OUT}), .CS(1'b1), .WE(1'b0), .OE(1'b1), .D({FIM, eeprom_2_d, RAM_IN, MQ_OUT_t, MQ_IN}));

  // Other names for the same wires on the sheet: EPR[5:0] = {IR_OUT[2:0], S_OUT}; Op[2:0] = IR_OUT[2:0];
  //   Q1[7:0] = IR_OUT; Q2[7:0] = MAR_OUT; S[2:0] = S_OUT; VALOR_AC[7:0] = AC_OUT

  // Notes on the sheet:
  //   contents of rom_1 (hex, n*v repeats v):
  //   24,25,0,0,5,3
  //   contents of eeprom_1 (hex, n*v repeats v):
  //   3,c,10,2,24,40,0,0,3,c,10,2,24,40,0,0,3,c,10,2,24,40,0,0,3,c,10
  //   ,2,24,40,0,0,3,c,10,40,4*0,3,c,10,40,4*0,3,c,10,2,44,0,0,0,3,c
  //   ,10,2,80
  //   contents of eeprom_2 (hex, n*v repeats v):
  //   6*0,80,7*0,80,6*0,1,80,6*0,1,80,5*0,80,7*0,80,8*0,80,6*0,4,80
endmodule
