// Digital circuit cp.dig as structural Verilog
module cp (
  input  [2:0] Opcode,
  input  [7:0] B,
  input  [7:0] A,
  input  CLOCK,
  input  G
);

  wire D0, D1, D2, D3, D4, D5, D6, D7;

  Demultiplexer #(.Selector_Bits(3)) demultiplexer_1 (
    .sel(Opcode), .in(1'b1), .out_0(D0), .out_1(D1), .out_2(D2), .out_3(D3), .out_4(D4), .out_5(D5),
    .out_6(D6), .out_7(D7));
  ALU8bits alu8bits_1 ();  // open: Opcode, B, A, RAC, RMQ

  // Other names for the same wires on the sheet: CLK = CLOCK; Op[2:0] = Opcode; Op1 = Opcode[0]; Op2 = Opcode[1];
  //   Op3 = Opcode[2]
endmodule
