// Digital circuit registradores8bits.dig as structural Verilog
module registradores8bits (
  input  [7:0] A,
  input  [7:0] B,
  output [7:0] AC,
  output [7:0] MQ
);

  // multiplicador8bits_v2 multiplicador8bits_v2_1: pin names not known; wires that end beside it: A, B, {MQ, AC}

  // Other names for the same wires on the sheet: R[15:0] = {MQ, AC}; R1[7:0] = AC; R2[7:0] = MQ
endmodule
