// Digital circuit shiftleftac8bits.dig as structural Verilog
module shiftleftac8bits (
  input  [7:0] A,
  input  [7:0] B,
  input  Op,
  output Cout,
  output [7:0] NAND8BITS,
  output [7:0] XOR8BITS,
  output [7:0] SHIFTRIGHT,
  output [7:0] SHIFTLEFT,
  output [7:0] S
);

  wire C1;
  wire [3:0] BL, BM;
  wire [7:0] R;

  assign NAND8BITS = ~(A & B);  // NAnd nand_1, 8 bits wide
  assign XOR8BITS = A ^ B;  // XOr xor_1, 8 bits wide
  Multiplexer #(.Bits(8)) multiplexer_1 (.sel(Op), .in_0(B), .in_1(R), .out({BM, BL}));
  assign R = ~B;  // Not not_1, 8 bits wide
  // somador4bits somador4bits_1: pin names not known; wires that end beside it: A[3:0], BL, Op, C1, S[3:0]
  // somador4bits somador4bits_2: pin names not known; wires that end beside it: A[7:4], BM, C1, Cout, S[7:4]
  Seven_Seg_Hex seven_seg_hex_1 (.d(S[7:4]), .dp(1'b0));
  Seven_Seg_Hex seven_seg_hex_2 (.d(S[3:0]), .dp(1'b0));

  assign SHIFTLEFT = {A[6:0], 1'b0};
  assign SHIFTRIGHT = {1'b0, A[7:1]};

  // Other names for the same wires on the sheet: A1 = A[0]; A3[6:0] = A[6:0]; AC[7:0] = A; AL[3:0] = A[3:0];
  //   SL[7:1] = A[6:0]; A2[6:0] = A[7:1]; SR[6:0] = A[7:1]; AM[3:0] = A[7:4]; A4 = A[7]; N[7:0] = B;
  //   RN[7:0] = NAND8BITS; RX[7:0] = XOR8BITS; S1[3:0] = S[3:0]; S2[3:0] = S[7:4]
endmodule
