// Digital circuit subtrator8bits.dig as structural Verilog
module subtrator8bits (
  input  [7:0] A,
  input  [7:0] B,
  input  Op,
  output Cout,
  output [7:0] S
);

  wire C1;
  wire [3:0] BL, BM;
  wire [7:0] R;

  Multiplexer #(.Bits(8)) multiplexer_1 (.sel(Op), .in_0(B), .in_1(R), .out({BM, BL}));
  assign R = ~B;  // Not not_1, 8 bits wide
  // somador4bits somador4bits_1: pin names not known; wires that end beside it: A[3:0], BL, Op, C1, S[3:0]
  // somador4bits somador4bits_2: pin names not known; wires that end beside it: A[7:4], BM, C1, Cout, S[7:4]
  Seven_Seg_Hex seven_seg_hex_1 (.d(S[7:4]), .dp(1'b0));
  Seven_Seg_Hex seven_seg_hex_2 (.d(S[3:0]), .dp(1'b0));

  // Other names for the same wires on the sheet: AL[3:0] = A[3:0]; AM[3:0] = A[7:4]; S1[3:0] = S[3:0];
  //   S2[3:0] = S[7:4]
endmodule
